// Logisim project control-logic.circ as structural Verilog: 1 circuit, main circuit control_logic
module control_logic (
  input  [31:0] Instruction,
  input  BrEq,
  input  BrLt,
  output PCSel,
  output RegWEn,
  output [2:0] ImmSel,
  output BrUn,
  output ASel,
  output BSel,
  output [3:0] ALUSel,
  output MemWEn,
  output [1:0] WBSel
);

  wire and_34_out, and_35_out, and_36_out, and_37_out, and_38_out, and_39_out, comparator_1_eq,
       comparator_2_eq, comparator_3_eq, comparator_4_eq, comparator_5_eq, comparator_6_eq, comparator_7_eq,
       comparator_8_eq, comparator_9_eq, comparator_18_eq, comparator_19_eq, comparator_20_eq,
       comparator_21_eq, comparator_22_eq, comparator_23_eq, comparator_24_eq, comparator_25_eq,
       comparator_26_eq, comparator_27_eq, comparator_28_eq, comparator_29_eq, comparator_30_eq,
       comparator_31_eq, comparator_32_eq, comparator_33_eq, comparator_34_eq, comparator_35_eq,
       comparator_36_eq, comparator_37_eq, comparator_38_eq, comparator_39_eq, comparator_40_eq,
       comparator_41_eq, comparator_42_eq, comparator_43_eq, comparator_44_eq, comparator_45_eq,
       comparator_46_eq, comparator_47_eq, comparator_48_eq, comparator_49_eq, comparator_50_eq,
       comparator_51_eq, is_add, is_addi, is_and, is_andi, is_auipc, is_beq, is_bge, is_bgeu, is_blt,
       is_bltu, is_bne, is_Btype, is_Itype, is_jal, is_jalr, is_lb, is_lh, is_load, is_lui, is_lw, is_mul,
       is_mulh, is_mulhu, is_or, is_ori, is_Rtype, is_sb, is_sh, is_sll, is_slli, is_slt, is_slti, is_sra,
       is_srai, is_srl, is_srli, is_Stype, is_sub, is_sw, is_xor, is_xori, not_1_out, not_2_out, not_3_out,
       not_4_out, or_1_out;
  wire [5:0] rom_input;
  wire [15:14] rom_1_data;

  Comparator #(.width(3)) comparator_1 (.a(Instruction[14:12]), .b(3'b000), .eq(comparator_1_eq));  // open: gt, lt
  Comparator #(.width(3)) comparator_2 (.a(Instruction[14:12]), .b(3'b001), .eq(comparator_2_eq));  // open: gt, lt
  Comparator #(.width(3)) comparator_3 (.a(Instruction[14:12]), .b(3'b010), .eq(comparator_3_eq));  // open: gt, lt
  Comparator #(.width(3)) comparator_4 (.a(Instruction[14:12]), .b(3'b100), .eq(comparator_4_eq));  // open: gt, lt
  Comparator #(.width(3)) comparator_5 (.a(Instruction[14:12]), .b(3'b101), .eq(comparator_5_eq));  // open: gt, lt
  Comparator #(.width(3)) comparator_6 (.a(Instruction[14:12]), .b(3'b110), .eq(comparator_6_eq));  // open: gt, lt
  Comparator #(.width(3)) comparator_7 (.a(Instruction[14:12]), .b(3'b111), .eq(comparator_7_eq));  // open: gt, lt
  ROM #(.addrWidth(6), .dataWidth(16)) rom_1 (
    .addr(rom_input), .data({rom_1_data, WBSel, MemWEn, ALUSel, BSel, ASel, BrUn, ImmSel, RegWEn}));
  and and_1 (is_addi, is_Itype, comparator_1_eq);
  and and_2 (is_slli, is_Itype, comparator_2_eq);
  and and_3 (is_slti, is_Itype, comparator_3_eq);
  and and_4 (is_xori, is_Itype, comparator_4_eq);
  and and_5 (is_ori, is_Itype, comparator_6_eq);
  and and_6 (is_andi, is_Itype, comparator_7_eq);
  Comparator #(.width(7)) comparator_8 (.a(Instruction[31:25]), .b({7{1'b0}}), .eq(comparator_8_eq));  // open: gt, lt
  Comparator #(.width(7)) comparator_9 (.a(7'b0100000), .b(Instruction[31:25]), .eq(comparator_9_eq));  // open: gt, lt
  and and_7 (is_srli, comparator_5_eq, is_Itype, comparator_8_eq);
  and and_8 (is_srai, comparator_5_eq, comparator_9_eq);
  Priority_Encoder #(.select_enc(6)) priority_encoder_1 (
    .in0(is_add), .in1(is_mul), .in2(is_sub), .in3(is_sll), .in4(is_mulh), .in5(is_mulhu), .in6(is_slt),
    .in7(is_xor), .in8(is_srl), .in9(is_sra), .in10(is_or), .in11(is_and), .in12(is_lb), .in13(is_lh),
    .in14(is_lw), .in15(is_addi), .in16(is_slli), .in17(is_slti), .in18(is_xori), .in19(is_srli),
    .in20(is_srai), .in21(is_ori), .in22(is_andi), .in23(is_sb), .in24(is_sh), .in25(is_sw), .in26(is_beq),
    .in27(is_bne), .in28(is_blt), .in29(is_bge), .in30(is_bltu), .in31(is_bgeu), .in32(is_auipc),
    .in33(is_lui), .in34(is_jal), .in35(is_jalr), .out(rom_input));  // open: in36, in37, in38, in39, in40, in41, in42, in43, in44, in45, in46, in47, in48, in49, in50, in51, in52, in53, in54, in55, in56, in57, in58, in59, in60, in61, in62, in63, gs, en_out, en_in
  Comparator #(.width(7)) comparator_10 (.a(Instruction[6:0]), .b(7'b0110011), .eq(is_Rtype));  // open: gt, lt
  Comparator #(.width(7)) comparator_11 (.a(Instruction[6:0]), .b(7'b0010011), .eq(is_Itype));  // open: gt, lt
  Comparator #(.width(7)) comparator_12 (.a(Instruction[6:0]), .b(7'b1100011), .eq(is_Btype));  // open: gt, lt
  Comparator #(.width(7)) comparator_13 (.a(Instruction[6:0]), .b(7'b0100011), .eq(is_Stype));  // open: gt, lt
  Comparator #(.width(7)) comparator_14 (.a(Instruction[6:0]), .b(7'b0010111), .eq(is_auipc));  // open: gt, lt
  Comparator #(.width(7)) comparator_15 (.a(Instruction[6:0]), .b(7'b0110111), .eq(is_lui));  // open: gt, lt
  Comparator #(.width(7)) comparator_16 (.a(Instruction[6:0]), .b(7'b1101111), .eq(is_jal));  // open: gt, lt
  Comparator #(.width(7)) comparator_17 (.a(Instruction[6:0]), .b(7'b0000011), .eq(is_load));  // open: gt, lt
  Comparator #(.width(3)) comparator_18 (.a(Instruction[14:12]), .b(3'b110), .eq(comparator_18_eq));  // open: gt, lt
  Comparator #(.width(3)) comparator_19 (.a(Instruction[14:12]), .b(3'b111), .eq(comparator_19_eq));  // open: gt, lt
  Comparator #(.width(3)) comparator_20 (.a(Instruction[14:12]), .b(3'b000), .eq(comparator_20_eq));  // open: gt, lt
  Comparator #(.width(3)) comparator_21 (.a(Instruction[14:12]), .b(3'b001), .eq(comparator_21_eq));  // open: gt, lt
  Comparator #(.width(3)) comparator_22 (.a(Instruction[14:12]), .b(3'b011), .eq(comparator_22_eq));  // open: gt, lt
  Comparator #(.width(3)) comparator_23 (.a(Instruction[14:12]), .b(3'b010), .eq(comparator_23_eq));  // open: gt, lt
  Comparator #(.width(3)) comparator_24 (.a(Instruction[14:12]), .b(3'b100), .eq(comparator_24_eq));  // open: gt, lt
  Comparator #(.width(3)) comparator_25 (.a(Instruction[14:12]), .b(3'b101), .eq(comparator_25_eq));  // open: gt, lt
  Comparator #(.width(7)) comparator_26 (.a(Instruction[31:25]), .b({7{1'b0}}), .eq(comparator_26_eq));  // open: gt, lt
  Comparator #(.width(7)) comparator_27 (
    .a(Instruction[31:25]), .b(7'b0000001), .eq(comparator_27_eq));  // open: gt, lt
  Comparator #(.width(7)) comparator_28 (
    .a(Instruction[31:25]), .b(7'b0100000), .eq(comparator_28_eq));  // open: gt, lt
  Comparator #(.width(7)) comparator_29 (.a(Instruction[31:25]), .b({7{1'b0}}), .eq(comparator_29_eq));  // open: gt, lt
  Comparator #(.width(7)) comparator_30 (
    .a(Instruction[31:25]), .b(7'b0000001), .eq(comparator_30_eq));  // open: gt, lt
  Comparator #(.width(7)) comparator_31 (
    .a(Instruction[31:25]), .b(7'b0000001), .eq(comparator_31_eq));  // open: gt, lt
  Comparator #(.width(7)) comparator_32 (.a(Instruction[31:25]), .b({7{1'b0}}), .eq(comparator_32_eq));  // open: gt, lt
  Comparator #(.width(7)) comparator_33 (.a(Instruction[31:25]), .b({7{1'b0}}), .eq(comparator_33_eq));  // open: gt, lt
  Comparator #(.width(7)) comparator_34 (.a(Instruction[31:25]), .b({7{1'b0}}), .eq(comparator_34_eq));  // open: gt, lt
  Comparator #(.width(7)) comparator_35 (
    .a(Instruction[31:25]), .b(7'b0100000), .eq(comparator_35_eq));  // open: gt, lt
  Comparator #(.width(7)) comparator_36 (.a(Instruction[31:25]), .b({7{1'b0}}), .eq(comparator_36_eq));  // open: gt, lt
  Comparator #(.width(7)) comparator_37 (.a(Instruction[31:25]), .b({7{1'b0}}), .eq(comparator_37_eq));  // open: gt, lt
  Comparator #(.width(7)) comparator_38 (.a(Instruction[6:0]), .b(7'b1100111), .eq(comparator_38_eq));  // open: gt, lt
  Comparator #(.width(3)) comparator_39 (.a(Instruction[14:12]), .b(3'b000), .eq(comparator_39_eq));  // open: gt, lt
  and and_9 (is_jalr, comparator_38_eq, comparator_39_eq);
  and and_10 (is_add, comparator_20_eq, is_Rtype, comparator_26_eq);
  and and_11 (is_sll, comparator_21_eq, is_Rtype, comparator_29_eq);
  and and_12 (is_mulh, comparator_21_eq, is_Rtype, comparator_30_eq);
  and and_13 (is_mulhu, comparator_22_eq, is_Rtype, comparator_31_eq);
  and and_14 (is_slt, comparator_23_eq, is_Rtype, comparator_32_eq);
  and and_15 (is_xor, comparator_24_eq, is_Rtype, comparator_33_eq);
  and and_16 (is_srl, comparator_25_eq, is_Rtype, comparator_34_eq);
  and and_17 (is_sra, comparator_25_eq, is_Rtype, comparator_35_eq);
  and and_18 (is_or, comparator_18_eq, is_Rtype, comparator_36_eq);
  and and_19 (is_and, comparator_19_eq, is_Rtype, comparator_37_eq);
  and and_20 (is_mul, comparator_20_eq, is_Rtype, comparator_27_eq);
  and and_21 (is_sub, comparator_20_eq, is_Rtype, comparator_28_eq);
  Comparator #(.width(3)) comparator_40 (.a(Instruction[14:12]), .b(3'b000), .eq(comparator_40_eq));  // open: gt, lt
  Comparator #(.width(3)) comparator_41 (.a(Instruction[14:12]), .b(3'b001), .eq(comparator_41_eq));  // open: gt, lt
  Comparator #(.width(3)) comparator_42 (.a(Instruction[14:12]), .b(3'b100), .eq(comparator_42_eq));  // open: gt, lt
  Comparator #(.width(3)) comparator_43 (.a(Instruction[14:12]), .b(3'b101), .eq(comparator_43_eq));  // open: gt, lt
  Comparator #(.width(3)) comparator_44 (.a(Instruction[14:12]), .b(3'b110), .eq(comparator_44_eq));  // open: gt, lt
  Comparator #(.width(3)) comparator_45 (.a(Instruction[14:12]), .b(3'b111), .eq(comparator_45_eq));  // open: gt, lt
  Comparator #(.width(3)) comparator_46 (.a(Instruction[14:12]), .b(3'b000), .eq(comparator_46_eq));  // open: gt, lt
  Comparator #(.width(3)) comparator_47 (.a(Instruction[14:12]), .b(3'b001), .eq(comparator_47_eq));  // open: gt, lt
  Comparator #(.width(3)) comparator_48 (.a(Instruction[14:12]), .b(3'b010), .eq(comparator_48_eq));  // open: gt, lt
  Comparator #(.width(3)) comparator_49 (.a(Instruction[14:12]), .b(3'b000), .eq(comparator_49_eq));  // open: gt, lt
  Comparator #(.width(3)) comparator_50 (.a(Instruction[14:12]), .b(3'b001), .eq(comparator_50_eq));  // open: gt, lt
  Comparator #(.width(3)) comparator_51 (.a(Instruction[14:12]), .b(3'b010), .eq(comparator_51_eq));  // open: gt, lt
  and and_22 (is_beq, is_Btype, comparator_40_eq);
  and and_23 (is_bne, is_Btype, comparator_41_eq);
  and and_24 (is_blt, is_Btype, comparator_42_eq);
  and and_25 (is_bge, is_Btype, comparator_43_eq);
  and and_26 (is_bltu, is_Btype, comparator_44_eq);
  and and_27 (is_bgeu, is_Btype, comparator_45_eq);
  and and_28 (is_lb, is_load, comparator_46_eq);
  and and_29 (is_lh, is_load, comparator_47_eq);
  and and_30 (is_lw, is_load, comparator_48_eq);
  and and_31 (is_sb, is_Stype, comparator_49_eq);
  and and_32 (is_sh, is_Stype, comparator_50_eq);
  and and_33 (is_sw, is_Stype, comparator_51_eq);
  not not_1 (not_1_out, BrLt);
  not not_2 (not_2_out, BrEq);
  not not_3 (not_3_out, BrUn);
  not not_4 (not_4_out, BrUn);
  and and_34 (and_34_out, is_beq, BrEq);
  and and_35 (and_35_out, not_2_out, is_bne);
  and and_36 (and_36_out, is_blt, not_3_out, BrLt);
  and and_37 (and_37_out, BrLt, is_bltu, BrUn);
  and and_38 (and_38_out, not_4_out, is_bge, not_1_out);
  and and_39 (and_39_out, not_1_out, is_bgeu, BrUn);
  or or_1 (or_1_out, and_34_out, and_35_out, and_36_out, and_37_out, and_38_out, and_39_out);
  or or_2 (PCSel, or_1_out, is_jalr, is_jal);

  // Other names for the same wires on the sheet: opcode[6:0] = Instruction[6:0]; fun3[2:0] = Instruction[14:12];
  //   fun7[6:0] = Instruction[31:25]

  // Notes on the sheet:
  //   INPUTS to your circuit
  //   Connect ROM Input here ->
  //   contents of rom_1 (hex, n*v repeats v):
  //   100f 140f 160f 108f 148f 158f 110f 120f 128f 168f 130f 138f 41 41 41 1041 10c1 1141 1241 12c1 16c1
  //   1341 13c1 1842 1842 1842 4*1064 1074 1074 1067 17c7 2069 2041
  //   ROM FOR CONTROL LOGIC
  //   DON'T CHANGE THE LOCATIONS OF THE INPUTS AND OUTPUTS!
  //   This is only if you choose to do the ROM option
  //   CONNECT
  //   WIRE
  //   TO
  //   USE
  //   ROM
  //   OUTPUT from your circuit
  //   Reminder: If using ROM, use combinational logic for PCSel
endmodule
