// Logisim project cpu.circ as structural Verilog: 1 circuit, main circuit cpu
module cpu (
  input  clk,
  input  [31:0] Instruction,
  input  [31:0] MemReadData,
  output [31:0] MemAddress,
  output [31:0] ProgramCounter,
  output [31:0] ra,
  output [31:0] sp,
  output [31:0] t0,
  output [31:0] t1,
  output [31:0] t2,
  output [31:0] s0,
  output [31:0] s1,
  output [31:0] a0,
  output [3:0] MemWriteMask,
  output [31:0] MemWriteData
);

  wire ASel, BEq, BLt, BSel, BUn, MemW, PCSel, RegWEn;
  wire [1:0] WBSel;
  wire [2:0] ImmSel;
  wire [3:0] ALUSel;
  wire [31:0] adder_1_out, adder_2_out, imm_gen_1_immediate, InstStage2, multiplexer_1_out,
       multiplexer_2_out, multiplexer_3_out, multiplexer_4_out, multiplexer_5_out, partial_load_1_datatoreg,
       PCStage2, regfile_1_readdata1, regfile_1_readdata2;

  Adder #(.width(32)) adder_1 (.a(ProgramCounter), .b(32'h4), .out(adder_1_out));  // open: cin, cout
  Register #(.width(32)) PC (.D(multiplexer_1_out), .clk(clk), .Q(ProgramCounter));  // open: en, clr
  Multiplexer #(.width(32)) multiplexer_1 (.in0(adder_1_out), .in1(MemAddress), .out(multiplexer_1_out), .sel(PCSel));
  Multiplexer #(.width(32)) multiplexer_2 (.in0(Instruction), .in1(32'h13), .out(multiplexer_2_out), .sel(PCSel));
  Register #(.width(32)) register_1 (.D(ProgramCounter), .clk(clk), .Q(PCStage2));  // open: en, clr
  Register #(.width(32)) register_2 (.D(multiplexer_2_out), .clk(clk), .Q(InstStage2));  // open: en, clr
  control_logic control_logic_1 (
    .Instruction(InstStage2), .BrEq(BEq), .BrLt(BLt), .PCSel(PCSel), .RegWEn(RegWEn), .ImmSel(ImmSel),
    .BrUn(BUn), .ASel(ASel), .BSel(BSel), .ALUSel(ALUSel), .MemWEn(MemW), .WBSel(WBSel));
  regfile regfile_1 (
    .ReadIndex1(InstStage2[19:15]), .ReadIndex2(InstStage2[24:20]), .WriteIndex(InstStage2[11:7]),
    .WriteData(multiplexer_5_out), .RegWEn(RegWEn), .clk(clk), .ra(ra), .sp(sp), .t0(t0), .t1(t1), .t2(t2),
    .s0(s0), .s1(s1), .a0(a0), .ReadData1(regfile_1_readdata1), .ReadData2(regfile_1_readdata2));
  imm_gen imm_gen_1 (.Instruction(InstStage2), .ImmSel(ImmSel), .Immediate(imm_gen_1_immediate));
  branch_comp branch_comp_1 (
    .BrData1(regfile_1_readdata1), .BrData2(regfile_1_readdata2), .BrUn(BUn), .BrEq(BEq), .BrLt(BLt));
  Multiplexer #(.width(32)) multiplexer_3 (
    .in0(regfile_1_readdata1), .in1(PCStage2), .out(multiplexer_3_out), .sel(ASel));
  Multiplexer #(.width(32)) multiplexer_4 (
    .in0(regfile_1_readdata2), .in1(imm_gen_1_immediate), .out(multiplexer_4_out), .sel(BSel));
  alu alu_1 (.A(multiplexer_3_out), .B(multiplexer_4_out), .ALUSel(ALUSel), .ALUResult(MemAddress));
  Adder #(.width(32)) adder_2 (.a(PCStage2), .b(32'h4), .out(adder_2_out));  // open: cin, cout
  partial_load partial_load_1 (
    .Instruction(InstStage2), .MemAddress(MemAddress), .DataFromMem(MemReadData),
    .DataToReg(partial_load_1_datatoreg));
  Multiplexer #(.select(2), .width(32)) multiplexer_5 (
    .in0(partial_load_1_datatoreg), .in1(MemAddress), .in2(adder_2_out), .out(multiplexer_5_out), .sel(WBSel));  // open: in3
  partial_store partial_store_1 (
    .Instruction(InstStage2), .MemAddress(MemAddress), .DataFromReg(regfile_1_readdata2), .MemWEn(MemW),
    .MemWriteMask(MemWriteMask), .DataToMem(MemWriteData));

  // Other names for the same wires on the sheet: rd[4:0] = InstStage2[11:7]; rs1[4:0] = InstStage2[19:15];
  //   rs2[4:0] = InstStage2[24:20]

  // Notes on the sheet:
  //   To IMEM
  //   IMEM (do **NOT** move this)
  //   From IMEM
  //   Inputs/Outputs for testing. Do **NOT** move these.
  //   It is OK to move the PC, RegFile, ALU, MEM, Branch Comp, Imm Gen, Partial Load, Partial Store and Control Logic to wherever is most convenient for you when constructing your CPU, and to delete this text
  //   To DMEM
  //   DMEM (do **NOT** move this)
  //   From DMEM
endmodule
