// Logisim project partial-load.circ as structural Verilog: 1 circuit, main circuit partial_load
module partial_load (
  input  [31:0] Instruction,
  input  [31:0] MemAddress,
  input  [31:0] DataFromMem,
  output [31:0] DataToReg
);

  wire is_lb, is_lh, is_lw;
  wire [1:0] load;
  wire [7:0] multiplexer_1_out;
  wire [15:0] multiplexer_2_out;
  wire [31:0] lb, lh;

  Comparator #(.mode("unsigned"), .width(3)) comparator_1 (
    .a(Instruction[14:12]), .b(3'b000), .eq(is_lb));  // open: gt, lt
  Comparator #(.mode("unsigned"), .width(3)) comparator_2 (
    .a(Instruction[14:12]), .b(3'b001), .eq(is_lh));  // open: gt, lt
  Comparator #(.mode("unsigned"), .width(3)) comparator_3 (
    .a(Instruction[14:12]), .b(3'b010), .eq(is_lw));  // open: gt, lt
  Multiplexer #(.select(2), .width(8)) multiplexer_1 (
    .in0(DataFromMem[7:0]), .in1(DataFromMem[15:8]), .in2(DataFromMem[23:16]), .in3(DataFromMem[31:24]),
    .out(multiplexer_1_out), .sel(MemAddress[1:0]));
  assign lb = {{24{multiplexer_1_out[7]}}, multiplexer_1_out};  // Bit_Extender bit_extender_1
  Multiplexer #(.select(2), .width(16)) multiplexer_2 (
    .in0(DataFromMem[15:0]), .in1(DataFromMem[23:8]), .in2(DataFromMem[31:16]), .out(multiplexer_2_out),
    .sel(MemAddress[1:0]));  // open: in3
  assign lh = {{16{multiplexer_2_out[15]}}, multiplexer_2_out};  // Bit_Extender bit_extender_2
  Priority_Encoder #(.select_enc(2)) priority_encoder_1 (
    .in0(is_lb), .in1(is_lh), .in2(is_lw), .out(load));  // open: in3, gs, en_out, en_in
  Multiplexer #(.select(2), .width(32)) multiplexer_3 (
    .in0(lb), .in1(lh), .in2(DataFromMem), .out(DataToReg), .sel(load));  // open: in3

  // Other names for the same wires on the sheet: byte0[7:0] = DataFromMem[7:0]; lw[31:0] = DataFromMem;
  //   byte1[7:0] = DataFromMem[15:8]; byte2[7:0] = DataFromMem[23:16]; byte3[7:0] = DataFromMem[31:24];
  //   fun3[2:0] = Instruction[14:12]; bits2[1:0] = MemAddress[1:0]

  // Notes on the sheet:
  //   INPUTS to your circuit
  //   DON'T CHANGE THE LOCATIONS OF THE INPUTS AND OUTPUTS!
  //   OUTPUT from your circuit
endmodule
