// Logisim project partial-store.circ as structural Verilog: 1 circuit, main circuit partial_store
module partial_store (
  input  [31:0] Instruction,
  input  [31:0] MemAddress,
  input  [31:0] DataFromReg,
  input  MemWEn,
  output [3:0] MemWriteMask,
  output [31:0] DataToMem
);

  wire comparator_4_eq, comparator_5_eq, comparator_6_eq, comparator_7_eq, comparator_8_eq, comparator_9_eq,
       is_sb, is_sb0, is_sb1, is_sb2, is_sb3, is_sh, is_sh0, is_sh1, is_sw;
  wire [1:0] store;
  wire [3:0] priority_encoder_2_out;
  wire [4:0] multiplexer_2_out;
  wire [31:0] bit_extender_1_out, bit_extender_2_out, sb, sh;

  Comparator #(.mode("unsigned"), .width(3)) comparator_1 (
    .a(Instruction[14:12]), .b(3'b000), .eq(is_sb));  // open: gt, lt
  Comparator #(.mode("unsigned"), .width(3)) comparator_2 (
    .a(Instruction[14:12]), .b(3'b001), .eq(is_sh));  // open: gt, lt
  Comparator #(.mode("unsigned"), .width(3)) comparator_3 (
    .a(Instruction[14:12]), .b(3'b010), .eq(is_sw));  // open: gt, lt
  Comparator #(.mode("unsigned"), .width(2)) comparator_4 (
    .a(MemAddress[1:0]), .b(2'b00), .eq(comparator_4_eq));  // open: gt, lt
  Comparator #(.mode("unsigned"), .width(2)) comparator_5 (
    .a(MemAddress[1:0]), .b(2'b01), .eq(comparator_5_eq));  // open: gt, lt
  Comparator #(.mode("unsigned"), .width(2)) comparator_6 (
    .a(MemAddress[1:0]), .b(2'b10), .eq(comparator_6_eq));  // open: gt, lt
  Comparator #(.mode("unsigned"), .width(2)) comparator_7 (
    .a(MemAddress[1:0]), .b(2'b11), .eq(comparator_7_eq));  // open: gt, lt
  Comparator #(.mode("unsigned"), .width(2)) comparator_8 (
    .a(MemAddress[1:0]), .b(2'b00), .eq(comparator_8_eq));  // open: gt, lt
  Comparator #(.mode("unsigned"), .width(2)) comparator_9 (
    .a(MemAddress[1:0]), .b(2'b10), .eq(comparator_9_eq));  // open: gt, lt
  and and_1 (is_sb0, is_sb, comparator_4_eq);
  and and_2 (is_sb1, is_sb, comparator_5_eq);
  and and_3 (is_sb2, is_sb, comparator_6_eq);
  and and_4 (is_sb3, is_sb, comparator_7_eq);
  and and_5 (is_sh0, is_sh, comparator_8_eq);
  and and_6 (is_sh1, is_sh, comparator_9_eq);
  Priority_Encoder #(.select_enc(2)) priority_encoder_1 (
    .in0(is_sb), .in1(is_sh), .in2(is_sw), .out(store));  // open: in3, gs, en_out, en_in
  assign bit_extender_1_out = {{24{1'b0}}, DataFromReg[7:0]};  // Bit_Extender bit_extender_1
  Multiplexer #(.select(2), .width(32)) multiplexer_1 (
    .in0(sb), .in1(sh), .in2(DataFromReg), .out(DataToMem), .sel(store));  // open: in3
  assign bit_extender_2_out = {{16{1'b0}}, DataFromReg[15:0]};  // Bit_Extender bit_extender_2
  Multiplexer #(.select(2), .width(5)) multiplexer_2 (
    .in0({5{1'b0}}), .in1(5'b01000), .in2(5'b10000), .in3(5'b11000), .out(multiplexer_2_out),
    .sel(MemAddress[1:0]));
  Shifter #(.width(32)) shifter_1 (.in(bit_extender_1_out), .\dist (multiplexer_2_out), .out(sb));
  Priority_Encoder #(.select_enc(4)) priority_encoder_2 (
    .in1(is_sb0), .in2(is_sb1), .in3(is_sh0), .in4(is_sb2), .in8(is_sb3), .in12(is_sh1), .in15(is_sw),
    .out(priority_encoder_2_out));  // open: in0, in5, in6, in7, in9, in10, in11, in13, in14, gs, en_out, en_in
  Shifter #(.width(32)) shifter_2 (.in(bit_extender_2_out), .\dist (multiplexer_2_out), .out(sh));
  Multiplexer #(.width(4)) multiplexer_3 (
    .in0(4'b0000), .in1(priority_encoder_2_out), .out(MemWriteMask), .sel(MemWEn));

  // Other names for the same wires on the sheet: byte0[7:0] = DataFromReg[7:0]; half_word[15:0] = DataFromReg[15:0];
  //   sw[31:0] = DataFromReg; fun3[2:0] = Instruction[14:12]; bits2[1:0] = MemAddress[1:0]

  // Notes on the sheet:
  //   INPUTS to your circuit
  //   DON'T CHANGE THE LOCATIONS OF THE INPUTS AND OUTPUTS!
  //   OUTPUT from your circuit
endmodule
