// Logisim project regfile.circ as structural Verilog: 1 circuit, main circuit regfile
module regfile (
  input  [4:0] ReadIndex1,
  input  [4:0] ReadIndex2,
  input  [4:0] WriteIndex,
  input  [31:0] WriteData,
  input  RegWEn,
  input  clk,
  output [31:0] ra,
  output [31:0] sp,
  output [31:0] t0,
  output [31:0] t1,
  output [31:0] t2,
  output [31:0] s0,
  output [31:0] s1,
  output [31:0] a0,
  output [31:0] ReadData1,
  output [31:0] ReadData2
);

  wire a0w, a1w, a2w, a3w, a4w, a5w, a6w, a7w, gpw, raw, s0w, s1w, s2w, s3w, s4w, s5w, s6w, s7w, s8w, s9w,
       s10w, s11w, spw, t0w, t1w, t2w, t3w, t4w, t5w, t6w, tpw;
  wire [31:0] a1, a2, a3, a4, a5, a6, a7, gp, s2, s3, s4, s5, s6, s7, s8, s9, s10, s11, t3, t4, t5, t6, tp,
       undriven;

  Register #(.width(32)) register_1 (.D(WriteData), .en(raw), .clk(clk), .Q(ra));  // open: clr
  Register #(.width(32)) register_2 (.D(WriteData), .en(spw), .clk(clk), .Q(sp));  // open: clr
  Register #(.width(32)) register_3 (.D(WriteData), .en(gpw), .clk(clk), .Q(gp));  // open: clr
  Register #(.width(32)) register_4 (.D(WriteData), .en(tpw), .clk(clk), .Q(tp));  // open: clr
  Register #(.width(32)) register_5 (.D(WriteData), .en(t0w), .clk(clk), .Q(t0));  // open: clr
  Register #(.width(32)) register_6 (.D(WriteData), .en(t1w), .clk(clk), .Q(t1));  // open: clr
  Register #(.width(32)) register_7 (.D(WriteData), .en(t2w), .clk(clk), .Q(t2));  // open: clr
  Register #(.width(32)) register_8 (.D(WriteData), .en(s0w), .clk(clk), .Q(s0));  // open: clr
  Register #(.width(32)) register_9 (.D(WriteData), .en(s1w), .clk(clk), .Q(s1));  // open: clr
  Register #(.width(32)) register_10 (.D(WriteData), .en(a0w), .clk(clk), .Q(a0));  // open: clr
  Register #(.width(32)) register_11 (.D(WriteData), .en(a1w), .clk(clk), .Q(a1));  // open: clr
  Register #(.width(32)) register_12 (.D(WriteData), .en(a2w), .clk(clk), .Q(a2));  // open: clr
  Register #(.width(32)) register_13 (.D(WriteData), .en(a3w), .clk(clk), .Q(a3));  // open: clr
  Register #(.width(32)) register_14 (.D(WriteData), .en(a4w), .clk(clk), .Q(a4));  // open: clr
  Register #(.width(32)) register_15 (.D(WriteData), .en(a5w), .clk(clk), .Q(a5));  // open: clr
  Register #(.width(32)) register_16 (.D(WriteData), .en(a6w), .clk(clk), .Q(a6));  // open: clr
  Register #(.width(32)) register_17 (.D(WriteData), .en(a7w), .clk(clk), .Q(a7));  // open: clr
  Register #(.width(32)) register_18 (.D(WriteData), .en(s2w), .clk(clk), .Q(s2));  // open: clr
  Register #(.width(32)) register_19 (.D(WriteData), .en(s3w), .clk(clk), .Q(s3));  // open: clr
  Register #(.width(32)) register_20 (.D(WriteData), .en(s4w), .clk(clk), .Q(s4));  // open: clr
  Register #(.width(32)) register_21 (.D(undriven), .en(s5w), .clk(clk), .Q(s5));  // open: clr
  Register #(.width(32)) register_22 (.D(WriteData), .en(s6w), .clk(clk), .Q(s6));  // open: clr
  Register #(.width(32)) register_23 (.D(WriteData), .en(s7w), .clk(clk), .Q(s7));  // open: clr
  Register #(.width(32)) register_24 (.D(WriteData), .en(s8w), .clk(clk), .Q(s8));  // open: clr
  Register #(.width(32)) register_25 (.D(WriteData), .en(s9w), .clk(clk), .Q(s9));  // open: clr
  Register #(.width(32)) register_26 (.D(WriteData), .en(s10w), .clk(clk), .Q(s10));  // open: clr
  Register #(.width(32)) register_27 (.D(WriteData), .en(s11w), .clk(clk), .Q(s11));  // open: clr
  Register #(.width(32)) register_28 (.D(WriteData), .en(t3w), .clk(clk), .Q(t3));  // open: clr
  Register #(.width(32)) register_29 (.D(WriteData), .en(t4w), .clk(clk), .Q(t4));  // open: clr
  Register #(.width(32)) register_30 (.D(WriteData), .en(t5w), .clk(clk), .Q(t5));  // open: clr
  Register #(.width(32)) register_31 (.D(WriteData), .en(t6w), .clk(clk), .Q(t6));  // open: clr
  Decoder #(.select(5)) decoder_1 (
    .out1(raw), .out2(spw), .out3(gpw), .out4(tpw), .out5(t0w), .out6(t1w), .out7(t2w), .out8(s0w),
    .out9(s1w), .out10(a0w), .out11(a1w), .out12(a2w), .out13(a3w), .out14(a4w), .out15(a5w), .out16(a6w),
    .out17(a7w), .out18(s2w), .out19(s3w), .out20(s4w), .out21(s5w), .out22(s6w), .out23(s7w), .out24(s8w),
    .out25(s9w), .out26(s10w), .out27(s11w), .out28(t3w), .out29(t4w), .out30(t5w), .out31(t6w),
    .sel(WriteIndex), .en(RegWEn));  // open: out0
  Multiplexer #(.select(5), .width(32)) multiplexer_1 (
    .in0({32{1'b0}}), .in1(ra), .in2(sp), .in3(gp), .in4(tp), .in5(t0), .in6(t1), .in7(t2), .in8(s0),
    .in9(s1), .in10(a0), .in11(a1), .in12(a2), .in13(a3), .in14(a4), .in15(a5), .in16(a6), .in17(a7),
    .in18(s2), .in19(s3), .in20(s4), .in21(s5), .in22(s6), .in23(s7), .in24(s8), .in25(s9), .in26(s10),
    .in27(s11), .in28(t3), .in29(t4), .in30(t5), .in31(t6), .out(ReadData1), .sel(ReadIndex1));
  Multiplexer #(.select(5), .width(32)) multiplexer_2 (
    .in0({32{1'b0}}), .in1(ra), .in2(sp), .in3(gp), .in4(tp), .in5(t0), .in6(t1), .in7(t2), .in8(s0),
    .in9(s1), .in10(a0), .in11(a1), .in12(a2), .in13(a3), .in14(a4), .in15(a5), .in16(a6), .in17(a7),
    .in18(s2), .in19(s3), .in20(s4), .in21(s5), .in22(s6), .in23(s7), .in24(s8), .in25(s9), .in26(s10),
    .in27(s11), .in28(t3), .in29(t4), .in30(t5), .in31(t6), .out(ReadData2), .sel(ReadIndex2));

  // Notes on the sheet:
  //   INPUTS to your circuit
  //   DON'T CHANGE THE LOCATIONS OF THE INPUTS AND OUTPUTS!
  //   These are DEBUG/TEST outputs from your circuit.
  //   OUTPUTS from your circuit
endmodule
